// Logisim project ALU.circ as structural Verilog
module _2LineMux (
  input  Ctrl,
  input  A,
  input  B,
  output out_4
);

  wire _0_out, _1_out, not_1_out;

  not not_1 (not_1_out, Ctrl);
  and _0 (_0_out, not_1_out, A);
  and _1 (_1_out, Ctrl, B);
  or or_1 (out_4, _0_out, _1_out);
endmodule

module _4LineMux (
  input  X,
  input  Y,
  input  A,
  input  B,
  input  C,
  input  D,
  output out_7
);

  wire _00_out, _01_out, _10_out, _11_out, not_1_out, not_2_out, not_3_out, not_4_out;

  not not_1 (not_1_out, X);
  not not_2 (not_2_out, Y);
  not not_3 (not_3_out, X);
  not not_4 (not_4_out, Y);
  and _00 (_00_out, not_1_out, not_2_out, A);
  and _01 (_01_out, not_3_out, Y, B);
  and _10 (_10_out, X, not_4_out, C);
  and _11 (_11_out, X, Y, D);
  or or_1 (out_7, _00_out, _01_out, _10_out, _11_out);
endmodule

module FullAdder (
  input  A,
  input  B,
  input  C_IN,
  output SUM,
  output C_OUT
);

  wire and_1_out, and_2_out, xor_1_out;

  xor xor_1 (xor_1_out, A, B);
  and and_1 (and_1_out, xor_1_out, C_IN);
  and and_2 (and_2_out, A, B);
  xor xor_2 (SUM, xor_1_out, C_IN);
  or or_1 (C_OUT, and_1_out, and_2_out);
endmodule

module ALU (
  input  CIN,
  input  ctrl,
  input  in_3,
  input  A,
  input  B,
  output Output,
  output Cout
);

  wire and_1_out, AND_2_out, fulladder_1_sum, n2linemux_1_out_4, not_1_out, OR_out;

  not not_1 (not_1_out, B);
  and and_1 (and_1_out, ctrl, in_3);
  _2LineMux u_2linemux_1 (.A(B), .B(not_1_out), .Ctrl(and_1_out), .out_4(n2linemux_1_out_4));
  FullAdder fulladder_1 (.A(CIN), .B(A), .C_IN(n2linemux_1_out_4), .SUM(fulladder_1_sum), .C_OUT(Cout));
  and AND_2 (AND_2_out, A, B);
  or OR (OR_out, A, B);
  _4LineMux u_4linemux_1 (
    .A(AND_2_out), .B(OR_out), .C(fulladder_1_sum), .D(fulladder_1_sum), .out_7(Output), .X(ctrl), .Y(in_3));

  // Notes on the sheet:
  //   Flip: 0=N 1=Y
endmodule

module Alu_test (
  input  A0,
  input  A1,
  input  B0,
  input  B1,
  input  in_5,
  input  in_6,
  output out_7,
  output out_8,
  output out_9
);

  wire alu_2_cout;

  ALU alu_1 (.A(A0), .B(B0), .Output(out_8), .CIN(alu_2_cout), .ctrl(in_5), .in_3(in_6), .Cout(out_7));
  ALU alu_2 (.A(A1), .B(B1), .Output(out_9), .CIN(in_6), .ctrl(in_5), .in_3(in_6), .Cout(alu_2_cout));
endmodule
