// Logisim project Adder.circ as structural Verilog
module HalfAdder (
  input  A,
  input  B,
  output sum,
  output Carry
);

  xor xor_1 (sum, A, B);
  and and_1 (Carry, A, B);
endmodule

module FullAdder (
  input  A,
  input  B,
  input  C_IN,
  output SUM,
  output C_OUT
);

  wire and_1_out, and_2_out, xor_1_out;

  xor xor_1 (xor_1_out, A, B);
  and and_1 (and_1_out, xor_1_out, C_IN);
  and and_2 (and_2_out, A, B);
  xor xor_2 (SUM, xor_1_out, C_IN);
  or or_1 (C_OUT, and_1_out, and_2_out);
endmodule

module _2bit_Adder (
  input  A1,
  input  A0,
  input  A2,
  input  B0,
  output out_5,
  output out_6,
  output out_7
);

  wire halfadder_1_carry;

  FullAdder fulladder_1 (.A(halfadder_1_carry), .B(A1), .C_IN(A2), .SUM(out_6), .C_OUT(out_5));
  HalfAdder halfadder_1 (.A(A0), .B(B0), .sum(out_7), .Carry(halfadder_1_carry));

  // Notes on the sheet:
  //   carryout
  //   sum2
  //   Sum1
endmodule
