// Logisim project CS240_PROJECT_SHI_CHENG.circ as structural Verilog: 7 circuits, main circuit 4bit Signed Multiplier
module HalfAdder (
  input  A,
  input  B,
  output sum,
  output Carry
);

  xor xor_1 (sum, A, B);
  and and_1 (Carry, A, B);
endmodule

module FullAdder (
  input  A,
  input  B,
  input  C_IN,
  output SUM,
  output C_OUT
);

  wire and_1_out, and_2_out, xor_1_out;

  xor xor_1 (xor_1_out, A, B);
  and and_1 (and_1_out, xor_1_out, C_IN);
  and and_2 (and_2_out, A, B);
  xor xor_2 (SUM, xor_1_out, C_IN);
  or or_1 (C_OUT, and_1_out, and_2_out);
endmodule

module _4bit_Adder (
  input  A3,
  input  A2,
  input  A1,
  input  A0,
  input  B3,
  input  B2,
  input  B1,
  input  B0,
  output out_9,
  output sum3,
  output sum2,
  output sum1,
  output Sum0
);

  wire fulladder_2_c_out, fulladder_3_c_out, halfadder_1_carry;

  FullAdder fulladder_1 (.A(fulladder_2_c_out), .B(A3), .C_IN(B3), .SUM(sum3), .C_OUT(out_9));
  FullAdder fulladder_2 (.A(fulladder_3_c_out), .B(A2), .C_IN(B2), .SUM(sum2), .C_OUT(fulladder_2_c_out));
  FullAdder fulladder_3 (.A(halfadder_1_carry), .B(A1), .C_IN(B1), .SUM(sum1), .C_OUT(fulladder_3_c_out));
  HalfAdder halfadder_1 (.A(A0), .B(B0), .sum(Sum0), .Carry(halfadder_1_carry));
endmodule

module _4x4_UnsignedMultiplier (
  input  B0,
  input  A3,
  input  A2,
  input  A1,
  input  A0,
  input  B1,
  input  B2,
  input  B3,
  output out_9,
  output out_10,
  output out_11,
  output out_12,
  output out_13,
  output out_14,
  output out_15,
  output out_16
);

  wire and_1_out, and_2_out, and_3_out, and_4_out, and_5_out, and_6_out, and_7_out, and_8_out, and_9_out,
       and_10_out, and_11_out, and_12_out, and_13_out, and_14_out, and_15_out, n4bit_adder_2_out_9,
       n4bit_adder_2_sum1, n4bit_adder_2_sum2, n4bit_adder_2_sum3, n4bit_adder_3_out_9, n4bit_adder_3_sum1,
       n4bit_adder_3_sum2, n4bit_adder_3_sum3;

  and and_1 (and_1_out, B3, A3);
  and and_2 (and_2_out, B2, A3);
  and and_3 (and_3_out, B2, A2);
  and and_4 (and_4_out, B3, A2);
  and and_5 (and_5_out, B1, A3);
  and and_6 (and_6_out, B2, A1);
  and and_7 (and_7_out, B3, A1);
  and and_8 (and_8_out, B1, A2);
  and and_9 (and_9_out, B1, A1);
  and and_10 (and_10_out, B2, A0);
  and and_11 (and_11_out, B3, A0);
  and and_12 (and_12_out, B1, A0);
  _4bit_Adder u_4bit_adder_1 (
    .A3(n4bit_adder_2_out_9), .A2(n4bit_adder_2_sum3), .A1(n4bit_adder_2_sum2), .A0(n4bit_adder_2_sum1),
    .B3(and_1_out), .B2(and_4_out), .B1(and_7_out), .B0(and_11_out), .out_9(out_9), .sum3(out_10),
    .sum2(out_11), .sum1(out_12), .Sum0(out_13));
  _4bit_Adder u_4bit_adder_2 (
    .A3(n4bit_adder_3_out_9), .A2(n4bit_adder_3_sum3), .A1(n4bit_adder_3_sum2), .A0(n4bit_adder_3_sum1),
    .B3(and_2_out), .B2(and_3_out), .B1(and_6_out), .B0(and_10_out), .out_9(n4bit_adder_2_out_9),
    .sum3(n4bit_adder_2_sum3), .sum2(n4bit_adder_2_sum2), .sum1(n4bit_adder_2_sum1), .Sum0(out_14));
  and and_13 (and_13_out, B0, A3);
  _4bit_Adder u_4bit_adder_3 (
    .A3(1'b0), .A2(and_13_out), .A1(and_15_out), .A0(and_14_out), .B3(and_5_out), .B2(and_8_out),
    .B1(and_9_out), .B0(and_12_out), .out_9(n4bit_adder_3_out_9), .sum3(n4bit_adder_3_sum3),
    .sum2(n4bit_adder_3_sum2), .sum1(n4bit_adder_3_sum1), .Sum0(out_15));
  and and_14 (and_14_out, B0, A1);
  and and_15 (and_15_out, B0, A2);
  and and_16 (out_16, B0, A0);

  // Notes on the sheet:
  //   0
endmodule

module _4bit_Signed_Multiplier (
  input  in_1,
  input  in_2,
  input  in_3,
  input  in_4,
  input  in_5,
  input  _4Bit_IN,
  input  in_7,
  input  in_8,
  output out_9,
  output out_10,
  output out_11,
  output out_12,
  output out_13,
  output out_14,
  output out_15,
  output out_16
);

  wire ctrled_2scomp_4bitinverter_1_out_7, ctrled_2scomp_4bitinverter_1_out_8,
       ctrled_2scomp_4bitinverter_1_out_9, ctrled_2scomp_4bitinverter_1_out_10,
       ctrled_2scomp_4bitinverter_2_out_7, ctrled_2scomp_4bitinverter_2_out_8,
       ctrled_2scomp_4bitinverter_2_out_9, ctrled_2scomp_4bitinverter_2_out_10,
       n4x4_unsignedmultiplier_1_out_9, n4x4_unsignedmultiplier_1_out_10, n4x4_unsignedmultiplier_1_out_11,
       n4x4_unsignedmultiplier_1_out_12, n4x4_unsignedmultiplier_1_out_13, n4x4_unsignedmultiplier_1_out_14,
       n4x4_unsignedmultiplier_1_out_15, n4x4_unsignedmultiplier_1_out_16, xor_1_out;

  xor xor_1 (xor_1_out, in_5, in_1);
  Ctrled_2sComp_4BitInverter ctrled_2scomp_4bitinverter_1 (
    .Control(in_1), .in_1(in_1), .in_2(in_2), ._4Bit_IN(in_3), .in_4(in_4),
    .out_7(ctrled_2scomp_4bitinverter_1_out_7), .out_8(ctrled_2scomp_4bitinverter_1_out_8),
    .out_9(ctrled_2scomp_4bitinverter_1_out_9), .out_10(ctrled_2scomp_4bitinverter_1_out_10));  // open: Overflow
  Ctrled_2sComp_8bit_Inverter ctrled_2scomp_8bit_inverter_1 (
    .Control(xor_1_out), .in_1(n4x4_unsignedmultiplier_1_out_9), .in_2(n4x4_unsignedmultiplier_1_out_10),
    .in_3(n4x4_unsignedmultiplier_1_out_11), .in_4(n4x4_unsignedmultiplier_1_out_12),
    .in_5(n4x4_unsignedmultiplier_1_out_13), .in_6(n4x4_unsignedmultiplier_1_out_14),
    .in_7(n4x4_unsignedmultiplier_1_out_15), .in_8(n4x4_unsignedmultiplier_1_out_16), .out_11(out_9),
    .out_12(out_10), .out_13(out_11), .out_14(out_12), .out_15(out_13), .out_16(out_14), .out_17(out_15),
    .out_18(out_16));  // open: Overflow
  _4x4_UnsignedMultiplier u_4x4_unsignedmultiplier_1 (
    .B0(ctrled_2scomp_4bitinverter_1_out_10), .B1(ctrled_2scomp_4bitinverter_1_out_9),
    .B2(ctrled_2scomp_4bitinverter_1_out_8), .B3(ctrled_2scomp_4bitinverter_1_out_7),
    .A3(ctrled_2scomp_4bitinverter_2_out_7), .A2(ctrled_2scomp_4bitinverter_2_out_8),
    .A1(ctrled_2scomp_4bitinverter_2_out_9), .A0(ctrled_2scomp_4bitinverter_2_out_10),
    .out_9(n4x4_unsignedmultiplier_1_out_9), .out_10(n4x4_unsignedmultiplier_1_out_10),
    .out_11(n4x4_unsignedmultiplier_1_out_11), .out_12(n4x4_unsignedmultiplier_1_out_12),
    .out_13(n4x4_unsignedmultiplier_1_out_13), .out_14(n4x4_unsignedmultiplier_1_out_14),
    .out_15(n4x4_unsignedmultiplier_1_out_15), .out_16(n4x4_unsignedmultiplier_1_out_16));
  Ctrled_2sComp_4BitInverter ctrled_2scomp_4bitinverter_2 (
    .Control(in_5), .in_1(in_5), .in_2(_4Bit_IN), ._4Bit_IN(in_7), .in_4(in_8),
    .out_7(ctrled_2scomp_4bitinverter_2_out_7), .out_8(ctrled_2scomp_4bitinverter_2_out_8),
    .out_9(ctrled_2scomp_4bitinverter_2_out_9), .out_10(ctrled_2scomp_4bitinverter_2_out_10));  // open: Overflow

  // Notes on the sheet:
  //   4Bit In
  //   8Bit out
endmodule

module Ctrled_2sComp_4BitInverter (
  input  in_1,
  input  in_2,
  input  _4Bit_IN,
  input  in_4,
  input  Control,
  output Overflow,
  output out_7,
  output out_8,
  output out_9,
  output out_10
);

  wire halfadder_2_carry, halfadder_3_carry, halfadder_4_carry, xor_1_out, xor_2_out, xor_3_out, xor_4_out;

  xor xor_1 (xor_1_out, Control, in_1);
  HalfAdder halfadder_1 (.A(halfadder_2_carry), .B(xor_1_out), .sum(out_7), .Carry(Overflow));
  xor xor_2 (xor_2_out, Control, in_2);
  xor xor_3 (xor_3_out, Control, _4Bit_IN);
  HalfAdder halfadder_2 (.A(halfadder_3_carry), .B(xor_2_out), .sum(out_8), .Carry(halfadder_2_carry));
  HalfAdder halfadder_3 (.A(halfadder_4_carry), .B(xor_3_out), .sum(out_9), .Carry(halfadder_3_carry));
  xor xor_4 (xor_4_out, Control, in_4);
  HalfAdder halfadder_4 (.A(Control), .B(xor_4_out), .sum(out_10), .Carry(halfadder_4_carry));

  // Notes on the sheet:
  //   4Bit out
  //   +1
endmodule

module Ctrled_2sComp_8bit_Inverter (
  input  in_1,
  input  in_2,
  input  in_3,
  input  in_4,
  input  in_5,
  input  in_6,
  input  in_7,
  input  in_8,
  input  Control,
  output Overflow,
  output out_11,
  output out_12,
  output out_13,
  output out_14,
  output out_15,
  output out_16,
  output out_17,
  output out_18
);

  wire halfadder_2_carry, halfadder_3_carry, halfadder_4_carry, halfadder_5_carry, halfadder_6_carry,
       halfadder_7_carry, halfadder_8_carry, xor_1_out, xor_2_out, xor_3_out, xor_4_out, xor_5_out,
       xor_6_out, xor_7_out, xor_8_out;

  xor xor_1 (xor_1_out, Control, in_1);
  HalfAdder halfadder_1 (.A(halfadder_2_carry), .B(xor_1_out), .sum(out_11), .Carry(Overflow));
  xor xor_2 (xor_2_out, Control, in_2);
  HalfAdder halfadder_2 (.A(halfadder_3_carry), .B(xor_2_out), .sum(out_12), .Carry(halfadder_2_carry));
  xor xor_3 (xor_3_out, Control, in_3);
  xor xor_4 (xor_4_out, Control, in_4);
  HalfAdder halfadder_3 (.A(halfadder_5_carry), .B(xor_3_out), .sum(out_13), .Carry(halfadder_3_carry));
  xor xor_5 (xor_5_out, Control, in_5);
  HalfAdder halfadder_4 (.A(halfadder_6_carry), .B(xor_5_out), .sum(out_15), .Carry(halfadder_4_carry));
  HalfAdder halfadder_5 (.A(halfadder_4_carry), .B(xor_4_out), .sum(out_14), .Carry(halfadder_5_carry));
  xor xor_6 (xor_6_out, Control, in_6);
  HalfAdder halfadder_6 (.A(halfadder_7_carry), .B(xor_6_out), .sum(out_16), .Carry(halfadder_6_carry));
  xor xor_7 (xor_7_out, Control, in_7);
  HalfAdder halfadder_7 (.A(halfadder_8_carry), .B(xor_7_out), .sum(out_17), .Carry(halfadder_7_carry));
  xor xor_8 (xor_8_out, Control, in_8);
  HalfAdder halfadder_8 (.A(Control), .B(xor_8_out), .sum(out_18), .Carry(halfadder_8_carry));

  // Notes on the sheet:
  //   8Bit IN
  //   8Bit out
  //   +1
endmodule
