// Logisim project Comparators.circ as structural Verilog
module _1BitComparator (
  input  A,
  input  B,
  output A_B,
  output A_B_2,
  output A_B_3
);

  wire not_1_out, not_3_out, xor_1_out;

  not not_1 (not_1_out, A);
  and and_1 (A_B, not_1_out, B);
  xor xor_1 (xor_1_out, A, B);
  not not_2 (A_B_2, xor_1_out);
  and and_2 (A_B_3, A, not_3_out);
  not not_3 (not_3_out, B);
endmodule

module _2BitComparator (
  input  A,
  input  in_2,
  input  B,
  input  in_4,
  output A_B,
  output A_B_2,
  output A_B_3
);

  _2BitLess u_2bitless_1 (.A(A), .in_2(in_2), .B(B), .in_4(in_4), .A_B(A_B));
  _2BitEqual u_2bitequal_1 (.A(A), .in_2(in_2), .B(B), .in_4(in_4), .A_B(A_B_2));
  _2BitGreater u_2bitgreater_1 (.A(A), .in_2(in_2), .B(B), .in_4(in_4), .A_B(A_B_3));

  // Notes on the sheet:
  //   <
  //   =
  //   >
endmodule

module _2BitEqual (
  input  A,
  input  in_2,
  input  B,
  input  in_4,
  output A_B
);

  wire not_1_out, not_2_out, xor_1_out, xor_2_out;

  xor xor_1 (xor_1_out, A, B);
  not not_1 (not_1_out, xor_1_out);
  and and_1 (A_B, not_1_out, not_2_out);
  xor xor_2 (xor_2_out, in_2, in_4);
  not not_2 (not_2_out, xor_2_out);
endmodule

module _2BitGreater (
  input  A,
  input  in_2,
  input  B,
  input  in_4,
  output A_B
);

  wire and_1_out, and_2_out, and_3_out, not_1_out, not_2_out, not_3_out, xor_1_out;

  not not_1 (not_1_out, B);
  and and_1 (and_1_out, A, not_1_out);
  or or_1 (A_B, and_1_out, and_3_out);
  xor xor_1 (xor_1_out, A, B);
  not not_2 (not_2_out, xor_1_out);
  not not_3 (not_3_out, in_4);
  and and_2 (and_2_out, in_2, not_3_out);
  and and_3 (and_3_out, not_2_out, and_2_out);
endmodule

module _2BitLess (
  input  A,
  input  in_2,
  input  B,
  input  in_4,
  output A_B
);

  wire and_1_out, and_2_out, and_3_out, not_1_out, not_2_out, not_3_out, xor_1_out;

  not not_1 (not_1_out, A);
  and and_1 (and_1_out, not_1_out, B);
  or or_1 (A_B, and_1_out, and_3_out);
  xor xor_1 (xor_1_out, A, B);
  not not_2 (not_2_out, xor_1_out);
  not not_3 (not_3_out, in_2);
  and and_2 (and_2_out, not_3_out, in_4);
  and and_3 (and_3_out, not_2_out, and_2_out);
endmodule
